# Fritzing sketch BasketPInfo (saved by Fritzing 0.7.12b)
breadboards: 1

parts:
  Arduino1 = Arduino
  OLED1 = 128x32 SPI Monochrome OLEDDisplay
  DHT1 = DHT11 Humitidy and Temperature Sensor
  R1 = 10k Ω Resistor [package=THT]

nets:
  N1: Arduino1.D13, OLED1.RST
  N2: Arduino1.D12, OLED1.CS
  N3: Arduino1.D11, OLED1.D/C
  N4: Arduino1.D10, OLED1.CLK
  N5: Arduino1.D9, OLED1.DATA
  N6: Arduino1.D7, DHT1.DATA, R1.Pin_1
  GND: Arduino1.GND, OLED1.GND
  VIN: OLED1.VIN, DHT1.VDD, R1.Pin_0

custom parts:
  128x32 SPI Monochrome OLEDDisplay: 128x32 SPI OLED Monochrome Display
  DHT11 Humitidy and Temperature Sensor: DHT11 Humidity and Temperature Sensor
